// Logisim project Test1.circ as structural Verilog: 1 circuit, main circuit main
module main (
  input  A,
  input  B,
  input  C,
  input  D
);

  wire nand_1_out, nand_2_out, nand_3_out, nand_4_out, nand_5_out;

  nand nand_1 (nand_1_out, B, C);
  nand nand_2 (nand_2_out, C, C);
  nand nand_3 (nand_3_out, A, nand_1_out);
  nand nand_4 (nand_4_out, nand_2_out, D);
  nand nand_5 (nand_5_out, nand_3_out, nand_4_out);
  // Probe on nand_5_out

  // Notes on the sheet:
  //   F = AC' + AB' + C'D
endmodule
