// Logisim project Test2.circ as structural Verilog: 1 circuit, main circuit main
module main (
  input  A,
  input  B,
  input  C,
  input  A_2,
  input  B_2,
  input  C_2
);

  wire nand_1_out, nand_2_out, nand_3_out, nand_4_out, nand_5_out, nand_6_out, nand_7_out, nand_8_out,
       nand_9_out, nand_10_out, nand_11_out, nand_12_out, nand_13_out, nand_14_out, nand_15_out, nand_16_out,
       nand_17_out, nand_18_out, nand_19_out;

  nand nand_1 (nand_1_out, B, B);
  nand nand_2 (nand_2_out, C, C);
  nand nand_3 (nand_3_out, B_2, C_2);
  nand nand_4 (nand_4_out, A, A);
  nand nand_5 (nand_5_out, B_2, nand_3_out);
  nand nand_6 (nand_6_out, nand_3_out, C_2);
  nand nand_7 (nand_7_out, nand_1_out, C);
  nand nand_8 (nand_8_out, B, nand_2_out);
  nand nand_9 (nand_9_out, nand_5_out, nand_6_out);
  nand nand_10 (nand_10_out, nand_7_out, nand_8_out);
  nand nand_11 (nand_11_out, A_2, nand_9_out);
  nand nand_12 (nand_12_out, nand_10_out, nand_10_out);
  nand nand_13 (nand_13_out, A_2, nand_11_out);
  nand nand_14 (nand_14_out, nand_11_out, nand_9_out);
  nand nand_15 (nand_15_out, nand_4_out, nand_12_out);
  nand nand_16 (nand_16_out, A, nand_10_out);
  nand nand_17 (nand_17_out, nand_13_out, nand_14_out);
  nand nand_18 (nand_18_out, nand_15_out, nand_16_out);
  // Probe on nand_18_out
  nand nand_19 (nand_19_out, nand_17_out, nand_17_out);
  // Probe on nand_19_out

  // Notes on the sheet:
  //   F = A'B'C' + A'BC + AB'C + ABC'
  //   F = not(AxorBxorC)
  //   F = A xor (not(B xor C))
endmodule
