// Logisim project lab2.circ as structural Verilog: 7 circuits, main circuit Not
module Not (
);

  wire nand_1_out, transistor_1_out;

  Transistor transistor_1 (.in(1'b1), .out(transistor_1_out), .gate(1'b0));
  Transistor #(.\type ("n")) transistor_2 (.in(1'b0), .out(transistor_1_out), .gate(1'b0));
  // Probe on transistor_1_out
  nand nand_1 (nand_1_out, 1'b1, 1'b1);
  // Probe on nand_1_out
endmodule

module Nor (
  input  in_1,
  input  in_2
);

  wire nand_1_out, nand_2_out, nand_3_out, nand_4_out, transistor_1_out, transistor_2_out;

  Transistor #(.\type ("n")) transistor_1 (.in(1'b0), .out(transistor_1_out), .gate(1'b0));
  nand nand_1 (nand_1_out, in_1, in_1);
  nand nand_2 (nand_2_out, in_2, in_2);
  Transistor transistor_2 (.in(1'b1), .out(transistor_2_out), .gate(1'b0));
  Transistor transistor_3 (.in(transistor_2_out), .out(transistor_1_out), .gate(1'b0));
  // Probe on transistor_1_out
  Transistor #(.\type ("n")) transistor_4 (.in(1'b0), .out(transistor_1_out), .gate(1'b0));
  nand nand_3 (nand_3_out, nand_1_out, nand_2_out);
  nand nand_4 (nand_4_out, nand_3_out, nand_3_out);
  // Probe on nand_4_out
endmodule

module Nand (
);

  wire transistor_1_out, transistor_3_out;

  Transistor transistor_1 (.in(1'b1), .out(transistor_1_out), .gate(1'b1));
  Transistor #(.\type ("n")) transistor_2 (.in(transistor_3_out), .out(transistor_1_out), .gate(1'b1));
  Transistor #(.\type ("n")) transistor_3 (.in(1'b0), .out(transistor_3_out), .gate(1'b0));
  Transistor transistor_4 (.in(1'b1), .out(transistor_1_out), .gate(1'b0));
  // Probe on transistor_1_out
endmodule

module And (
);

  wire nand_1_out, nand_2_out, transistor_1_out, transistor_4_out, transistor_5_out, transistor_8_out,
       transistor_9_out, transistor_11_out, transistor_12_out;

  Transistor transistor_1 (.in(1'b1), .out(transistor_1_out), .gate(1'b1));
  Transistor transistor_2 (.in(1'b1), .out(transistor_1_out), .gate(1'b1));
  Transistor #(.\type ("n")) transistor_3 (.in(transistor_4_out), .out(transistor_1_out), .gate(1'b1));
  Transistor #(.\type ("n")) transistor_4 (.in(1'b0), .out(transistor_4_out), .gate(1'b1));
  Transistor transistor_5 (.in(1'b1), .out(transistor_5_out), .gate(1'b0));
  Transistor transistor_6 (.in(1'b1), .out(transistor_5_out), .gate(1'b1));
  Transistor #(.\type ("n")) transistor_7 (.in(transistor_8_out), .out(transistor_5_out), .gate(1'b0));
  Transistor #(.\type ("n")) transistor_8 (.in(1'b0), .out(transistor_8_out), .gate(1'b1));
  Transistor transistor_9 (.in(1'b1), .out(transistor_9_out), .gate(transistor_1_out));
  Transistor #(.\type ("n")) transistor_10 (.in(transistor_11_out), .out(transistor_9_out), .gate(transistor_1_out));
  Transistor #(.\type ("n")) transistor_11 (.in(1'b0), .out(transistor_11_out), .gate(transistor_1_out));
  Transistor transistor_12 (.in(1'b1), .out(transistor_12_out), .gate(transistor_5_out));
  // Probe on transistor_12_out
  Transistor #(.\type ("n")) transistor_13 (.in(1'b0), .out(transistor_12_out), .gate(transistor_5_out));
  Transistor transistor_14 (.in(1'b1), .out(transistor_9_out), .gate(transistor_1_out));
  // Probe on transistor_9_out
  nand nand_1 (nand_1_out, 1'b1, 1'b1);
  nand nand_2 (nand_2_out, nand_1_out, nand_1_out);
  // Probe on nand_2_out

  // Notes on the sheet:
  //   NAND Imple
  //   Less Transistor
  //   NAND Gate
endmodule

module Or (
  input  in_1,
  input  in_2,
  output out_3
);

  wire nand_1_out, nand_2_out;

  nand nand_1 (nand_1_out, in_1, in_1);
  nand nand_2 (nand_2_out, in_2, in_2);
  nand nand_3 (out_3, nand_1_out, nand_2_out);
endmodule

module Xor (
  input  in_1,
  input  in_2,
  input  in_3,
  input  in_4,
  output out_5,
  output out_6
);

  wire nand_1_out, nand_2_out, nand_3_out, nand_4_out, nand_5_out, nand_6_out, nand_7_out;

  nand nand_1 (nand_1_out, in_1, in_2);
  nand nand_2 (nand_2_out, in_3, in_3);
  nand nand_3 (nand_3_out, in_4, in_4);
  nand nand_4 (nand_4_out, in_1, nand_1_out);
  nand nand_5 (nand_5_out, nand_1_out, in_2);
  nand nand_6 (nand_6_out, nand_2_out, in_4);
  nand nand_7 (nand_7_out, in_3, nand_3_out);
  nand nand_8 (out_5, nand_4_out, nand_5_out);
  nand nand_9 (out_6, nand_6_out, nand_7_out);
endmodule

module XNOR (
  input  in_1,
  input  in_2,
  output out_3
);

  wire nand_1_out, nand_2_out, nand_3_out, nand_4_out;

  nand nand_1 (nand_1_out, in_1, in_2);
  nand nand_2 (nand_2_out, in_1, nand_1_out);
  nand nand_3 (nand_3_out, nand_1_out, in_2);
  nand nand_4 (nand_4_out, nand_2_out, nand_3_out);
  nand nand_5 (out_3, nand_4_out, nand_4_out);
endmodule
