// Logisim project lab3.circ as structural Verilog: 3 circuits, main circuit half adder
module half_adder (
  input  A,
  input  B,
  input  in_3,
  input  in_4
);

  wire nand_1_out, nand_2_out, nand_3_out, nand_4_out, nand_5_out, nand_6_out, nand_7_out, nand_8_out,
       nand_9_out, nand_10_out, nand_11_out, nand_12_out;

  nand nand_1 (nand_1_out, in_3, in_4);
  nand nand_2 (nand_2_out, A, A);
  nand nand_3 (nand_3_out, B, B);
  nand nand_4 (nand_4_out, A, B);
  nand nand_5 (nand_5_out, in_3, nand_1_out);
  nand nand_6 (nand_6_out, nand_1_out, in_4);
  nand nand_7 (nand_7_out, nand_1_out, nand_1_out);
  nand nand_8 (nand_8_out, nand_2_out, B);
  nand nand_9 (nand_9_out, nand_3_out, A);
  nand nand_10 (nand_10_out, nand_4_out, nand_4_out);
  nand nand_11 (nand_11_out, nand_5_out, nand_6_out);
  // Probe on nand_11_out
  // Probe on nand_7_out
  nand nand_12 (nand_12_out, nand_8_out, nand_9_out);
  // Probe on nand_12_out
  // Probe on nand_10_out

  // Notes on the sheet:
  //   S
  //   C
  //   S
  //   C
endmodule

module full_adder (
  input  A,
  input  B,
  input  C,
  output S,
  output C_2
);

  wire nand_1_out, nand_2_out, nand_3_out, nand_4_out, nand_5_out, nand_6_out, nand_7_out;

  nand nand_1 (nand_1_out, A, B);
  nand nand_2 (nand_2_out, A, nand_1_out);
  nand nand_3 (nand_3_out, nand_1_out, B);
  nand nand_4 (nand_4_out, nand_2_out, nand_3_out);
  nand nand_5 (nand_5_out, nand_4_out, C);
  nand nand_6 (nand_6_out, nand_4_out, nand_5_out);
  nand nand_7 (nand_7_out, nand_5_out, C);
  nand nand_8 (C_2, nand_5_out, nand_1_out);
  nand nand_9 (S, nand_6_out, nand_7_out);
endmodule

module FULL_ADDER_CHAIN (
  input  A,
  input  B,
  input  in_3,
  input  A_2,
  input  B_2,
  input  A_3,
  input  B_3,
  output S,
  output S_2,
  output S_3,
  output C
);

  wire multiplexer_1_out, multiplexer_2_out, multiplexer_3_out, nand_1_out, nand_2_out, nand_3_out,
       nand_4_out, nand_5_out, nand_6_out, nand_7_out, nand_8_out, nand_9_out, nand_10_out, nand_11_out,
       nand_12_out, nand_13_out, nand_14_out, nand_15_out, nand_16_out, nand_17_out, nand_18_out,
       nand_19_out, nand_20_out, nand_21_out, nand_23_out, nand_24_out, not_1_out, not_2_out, not_3_out;

  not not_1 (not_1_out, B);
  Multiplexer multiplexer_1 (.in0(B), .in1(not_1_out), .out(multiplexer_1_out), .sel(in_3));  // open: en
  not not_2 (not_2_out, B_2);
  Multiplexer multiplexer_2 (.in0(B_2), .in1(not_2_out), .out(multiplexer_2_out), .sel(in_3));  // open: en
  not not_3 (not_3_out, B_3);
  Multiplexer multiplexer_3 (.in0(B_3), .in1(not_3_out), .out(multiplexer_3_out), .sel(in_3));  // open: en
  nand nand_1 (nand_1_out, A_3, multiplexer_3_out);
  nand nand_2 (nand_2_out, A, multiplexer_1_out);
  nand nand_3 (nand_3_out, A_2, multiplexer_2_out);
  nand nand_4 (nand_4_out, A, nand_2_out);
  nand nand_5 (nand_5_out, nand_2_out, multiplexer_1_out);
  nand nand_6 (nand_6_out, A_2, nand_3_out);
  nand nand_7 (nand_7_out, nand_3_out, multiplexer_2_out);
  nand nand_8 (nand_8_out, A_3, nand_1_out);
  nand nand_9 (nand_9_out, nand_1_out, multiplexer_3_out);
  nand nand_10 (nand_10_out, nand_4_out, nand_5_out);
  nand nand_11 (nand_11_out, nand_6_out, nand_7_out);
  nand nand_12 (nand_12_out, nand_8_out, nand_9_out);
  nand nand_13 (nand_13_out, nand_10_out, in_3);
  nand nand_14 (nand_14_out, nand_11_out, nand_18_out);
  nand nand_15 (nand_15_out, nand_12_out, nand_19_out);
  nand nand_16 (nand_16_out, nand_10_out, nand_13_out);
  nand nand_17 (nand_17_out, nand_13_out, in_3);
  nand nand_18 (nand_18_out, nand_13_out, nand_2_out);
  nand nand_19 (nand_19_out, nand_14_out, nand_3_out);
  nand nand_20 (nand_20_out, nand_12_out, nand_15_out);
  nand nand_21 (nand_21_out, nand_15_out, nand_19_out);
  nand nand_22 (C, nand_15_out, nand_1_out);
  nand nand_23 (nand_23_out, nand_11_out, nand_14_out);
  nand nand_24 (nand_24_out, nand_14_out, nand_18_out);
  nand nand_25 (S, nand_16_out, nand_17_out);
  nand nand_26 (S_2, nand_23_out, nand_24_out);
  nand nand_27 (S_3, nand_20_out, nand_21_out);
endmodule
