// Logisim project lab4.circ as structural Verilog: 5 circuits, main circuit SR Latch
module SR_Latch (
  input  S,
  input  R,
  input  S_prime,
  input  R_prime,
  output Q_prime,
  output Q
);

  wire nand_1_out, nand_2_out;

  nor nor_1 (Q_prime, S, Q);
  nor nor_2 (Q, Q_prime, R);
  nand nand_1 (nand_1_out, S_prime, nand_2_out);
  nand nand_2 (nand_2_out, nand_1_out, R_prime);
  // Probe on nand_1_out
  // Probe on nand_2_out

  // Notes on the sheet:
  //   Q'
  //   Q
endmodule

module D_Latch (
  input  D,
  output Q,
  output Q_prime
);

  wire clock_1_out, nand_1_out, nand_2_out;

  Clock clock_1 (.out(clock_1_out));
  nand nand_1 (nand_1_out, D, clock_1_out);
  nand nand_2 (nand_2_out, nand_1_out, clock_1_out);
  nand nand_3 (Q, nand_1_out, Q_prime);
  nand nand_4 (Q_prime, Q, nand_2_out);

  // Notes on the sheet:
  //   E
endmodule

module flip_flop (
  input  D
);

  wire clock_1_out, nand_1_out, nand_2_out, nand_3_out, nand_4_out, nand_5_out, nand_6_out, nand_7_out,
       nand_8_out, nand_9_out;

  nand nand_1 (nand_1_out, clock_1_out, clock_1_out);
  Clock clock_1 (.out(clock_1_out));
  nand nand_2 (nand_2_out, D, nand_1_out);
  nand nand_3 (nand_3_out, nand_2_out, nand_1_out);
  nand nand_4 (nand_4_out, nand_2_out, nand_5_out);
  nand nand_5 (nand_5_out, nand_4_out, nand_3_out);
  nand nand_6 (nand_6_out, nand_4_out, clock_1_out);
  nand nand_7 (nand_7_out, nand_6_out, clock_1_out);
  nand nand_8 (nand_8_out, nand_6_out, nand_9_out);
  nand nand_9 (nand_9_out, nand_8_out, nand_7_out);
  // Probe on nand_8_out
  // Probe on nand_9_out

  // Notes on the sheet:
  //   E
  //   Q
  //   Q'
endmodule

module Shift_register (
  input  D,
  output out_2,
  output out_3
);

  wire clock_1_out, nand_1_out, nand_2_out, nand_3_out, nand_4_out, nand_5_out, nand_6_out, nand_7_out,
       nand_8_out, nand_9_out, nand_10_out, nand_11_out, nand_12_out, nand_13_out, nand_14_out, nand_15_out,
       nand_16_out, nand_17_out, nand_18_out, nand_19_out, nand_20_out, nand_21_out, nand_23_out,
       nand_25_out, nand_26_out, nand_27_out;

  Clock clock_1 (.out(clock_1_out));
  nand nand_1 (nand_1_out, D, clock_1_out);
  nand nand_2 (nand_2_out, nand_1_out, clock_1_out);
  nand nand_3 (nand_3_out, out_2, clock_1_out);
  nand nand_4 (nand_4_out, nand_3_out, clock_1_out);
  nand nand_5 (nand_5_out, out_3, clock_1_out);
  nand nand_6 (nand_6_out, nand_5_out, clock_1_out);
  nand nand_7 (nand_7_out, clock_1_out, clock_1_out);
  nand nand_8 (nand_8_out, clock_1_out, clock_1_out);
  nand nand_9 (nand_9_out, clock_1_out, clock_1_out);
  nand nand_10 (nand_10_out, nand_1_out, nand_11_out);
  nand nand_11 (nand_11_out, nand_10_out, nand_2_out);
  nand nand_12 (nand_12_out, nand_3_out, nand_13_out);
  nand nand_13 (nand_13_out, nand_12_out, nand_4_out);
  nand nand_14 (nand_14_out, nand_5_out, nand_15_out);
  nand nand_15 (nand_15_out, nand_14_out, nand_6_out);
  nand nand_16 (nand_16_out, nand_10_out, nand_7_out);
  nand nand_17 (nand_17_out, nand_16_out, nand_7_out);
  nand nand_18 (nand_18_out, nand_12_out, nand_8_out);
  nand nand_19 (nand_19_out, nand_18_out, nand_8_out);
  nand nand_20 (nand_20_out, nand_14_out, nand_9_out);
  nand nand_21 (nand_21_out, nand_20_out, nand_9_out);
  nand nand_22 (out_2, nand_16_out, nand_23_out);
  nand nand_23 (nand_23_out, out_2, nand_17_out);
  nand nand_24 (out_3, nand_18_out, nand_25_out);
  nand nand_25 (nand_25_out, out_3, nand_19_out);
  nand nand_26 (nand_26_out, nand_20_out, nand_27_out);
  nand nand_27 (nand_27_out, nand_26_out, nand_21_out);
  // Probe on nand_26_out
  // Probe on nand_27_out

  // Notes on the sheet:
  //   E
  //   Q
  //   Q'
endmodule

module JK_flip_flop (
  input  Reset_prime,
  input  J,
  input  K,
  input  in_4,
  input  in_5,
  output out_6
);

  wire clock_1_out, clock_2_out, multiplexer_1_out, multiplexer_2_out, multiplexer_3_out, multiplexer_4_out,
       nand_1_out, nand_2_out, nand_3_out, nand_4_out, nand_5_out, nand_6_out, nand_7_out, nand_8_out,
       not_1_out, not_2_out;

  Clock clock_1 (.out(clock_1_out));
  Clock clock_2 (.out(clock_2_out));
  Multiplexer multiplexer_1 (.in0(nand_8_out), .in1(1'b0), .out(multiplexer_1_out), .sel(Reset_prime));  // open: en
  Multiplexer multiplexer_2 (.in0(J), .in1(1'b0), .out(multiplexer_2_out), .sel(Reset_prime));  // open: en
  not not_1 (not_1_out, clock_1_out);
  Multiplexer multiplexer_3 (.in0(K), .in1(1'b1), .out(multiplexer_3_out), .sel(Reset_prime));  // open: en
  Multiplexer multiplexer_4 (.in0(nand_7_out), .in1(1'b1), .out(multiplexer_4_out), .sel(Reset_prime));  // open: en
  J_K_Flip_Flop j_k_ff_1 (.J(in_4), .clk(clock_2_out), .K(in_5), .Q(out_6));  // open: Qn, preset, en, reset
  nand nand_1 (nand_1_out, multiplexer_1_out, not_1_out, multiplexer_2_out);
  nand nand_2 (nand_2_out, multiplexer_3_out, not_1_out, multiplexer_4_out);
  nand nand_3 (nand_3_out, nand_1_out, nand_4_out);
  nand nand_4 (nand_4_out, nand_3_out, nand_2_out);
  not not_2 (not_2_out, not_1_out);
  nand nand_5 (nand_5_out, nand_3_out, not_2_out);
  nand nand_6 (nand_6_out, not_2_out, nand_4_out);
  nand nand_7 (nand_7_out, nand_5_out, nand_8_out);
  nand nand_8 (nand_8_out, nand_7_out, nand_6_out);
  // Probe on nand_7_out
  // Probe on nand_8_out

  // Notes on the sheet:
  //   Clock
  //   Feedback X
  //   Feedback Y
endmodule
