// Logisim project Lock_FSM.circ as structural Verilog: 1 circuit, main circuit main
module main (
  input  Input
);

  wire clock_1_out, d_ff_1_q, d_ff_2_q, d_ff_3_q, nand_1_out, nand_2_out, nand_3_out, nand_4_out, nand_5_out,
       nand_6_out, nand_7_out, nand_8_out, nand_9_out, nand_10_out, nand_11_out, nand_12_out, nand_13_out,
       nand_14_out;

  nand nand_1 (nand_1_out, Input, Input);
  nand nand_2 (nand_2_out, d_ff_1_q, d_ff_1_q);
  nand nand_3 (nand_3_out, nand_9_out, d_ff_2_q);
  nand nand_4 (nand_4_out, Input, d_ff_1_q);
  nand nand_5 (nand_5_out, nand_1_out, nand_2_out);
  nand nand_6 (nand_6_out, nand_4_out, nand_4_out);
  nand nand_7 (nand_7_out, d_ff_2_q, d_ff_2_q);
  nand nand_8 (nand_8_out, Input, d_ff_1_q);
  nand nand_9 (nand_9_out, nand_5_out, nand_5_out);
  nand nand_10 (nand_10_out, nand_6_out, nand_7_out);
  nand nand_11 (nand_11_out, nand_8_out, nand_8_out);
  // Probe on nand_9_out
  nand nand_12 (nand_12_out, nand_11_out, d_ff_2_q);
  // Probe on nand_14_out
  nand nand_13 (nand_13_out, nand_12_out, nand_12_out);
  nand nand_14 (nand_14_out, nand_3_out, nand_10_out);
  Clock clock_1 (.out(clock_1_out));
  D_Flip_Flop d_ff_1 (.clk(clock_1_out), .D(nand_9_out), .Q(d_ff_1_q));  // open: Qn, preset, en, reset
  D_Flip_Flop d_ff_2 (.clk(clock_1_out), .D(nand_14_out), .Q(d_ff_2_q));  // open: Qn, preset, en, reset
  D_Flip_Flop d_ff_3 (.clk(clock_1_out), .D(nand_13_out), .Q(d_ff_3_q));  // open: Qn, preset, en, reset
  // Probe on d_ff_1_q
  // Probe on d_ff_2_q
  // Probe on d_ff_3_q

  // Notes on the sheet:
  //   Input
  //   S1(t)
  //   S0(t)
  //   S0(t+1)
  //   S1(t+1)
  //   Clk
  //   S0(t)
  //   S1(t)
  //   Unlock
endmodule
