// Logisim project Lock_FSM_template.circ as structural Verilog: 1 circuit, main circuit main
module main (
  input  Input
);

  wire and_1_out, and_2_out, and_3_out, and_4_out, clock_1_out, d_ff_1_q, d_ff_2_q, d_ff_3_q, not_1_out,
       not_2_out, not_3_out, or_1_out, or_2_out;

  not not_1 (not_1_out, d_ff_1_q);
  not not_2 (not_2_out, Input);
  not not_3 (not_3_out, d_ff_2_q);
  and and_1 (and_1_out, Input, not_1_out, not_3_out);
  and and_2 (and_2_out, not_2_out, not_1_out, d_ff_2_q);
  and and_3 (and_3_out, not_2_out, not_3_out, d_ff_1_q);
  or or_1 (or_1_out, and_1_out, and_2_out);
  and and_4 (and_4_out, d_ff_2_q, d_ff_1_q, Input);
  or or_2 (or_2_out, and_2_out, and_3_out);
  // Probe on or_1_out
  // Probe on or_2_out
  Clock clock_1 (.out(clock_1_out));
  D_Flip_Flop d_ff_1 (.clk(clock_1_out), .D(or_1_out), .Q(d_ff_1_q));  // open: Qn, preset, en, reset
  D_Flip_Flop d_ff_2 (.clk(clock_1_out), .D(or_2_out), .Q(d_ff_2_q));  // open: Qn, preset, en, reset
  D_Flip_Flop d_ff_3 (.clk(clock_1_out), .D(and_4_out), .Q(d_ff_3_q));  // open: Qn, preset, en, reset
  // Probe on d_ff_1_q
  // Probe on d_ff_2_q
  // Probe on d_ff_3_q

  // Notes on the sheet:
  //   Input
  //   S1(t)
  //   S0(t)
  //   S0(t+1)
  //   S1(t+1)
  //   Clk
  //   S0(t)
  //   S1(t)
  //   Unlock
endmodule
